// Logisim project CPU_Logic.circ as structural Verilog
module MUX (
  input  input_7,
  input  input_6,
  input  input_5,
  input  input_4,
  input  input_3,
  input  input_2,
  input  input_1,
  input  input_0
);

  // AND_Gate and_1 has open pins: in0=input_0, out=open
  // AND_Gate and_2 has open pins: in0=input_1, out=open
  // AND_Gate and_3 has open pins: in0=input_2, out=open
  // AND_Gate and_4 is placed but not wired
  // AND_Gate and_5 is placed but not wired
  // AND_Gate and_6 is placed but not wired
  // AND_Gate and_7 is placed but not wired
  // AND_Gate and_8 is placed but not wired
endmodule
